# Fritzing sketch oxymeter (saved by Fritzing 0.9.3b)

parts:
  Part1 = Arduino Uno (Rev3) - ICSP
  M1 = MAX30102
  Part2 = Adafruit BMP180
  L298N1 = L298N DC motor driver
  LCM1602_IIC1 = LCM1602 IIC [part_number="LCM1602 IIC" chip_label="LCM1602 IIC" package="DIP (Dual Inline) [THT]"]
  M2 = DC Motor
  VCC1 = Battery block 9V
  LCD1 = LCD screen
  S1 = Toggle Switch [package=THT]
  U1 = POT_SWITCH [package=pot_pth_switch]

nets:
  N1: Part1.A0, U1.G$2_1
  N2: Part1.A4/SDA, M1.SDA, Part2.SDA, LCM1602_IIC1.SDA
  N3: Part1.A5/SCL, M1.SCL, Part2.SCL, LCM1602_IIC1.SCL
  N4: Part1.D9_PWM, L298N1.ENA
  GND: Part1.GND, M1.GND, Part2.GND, L298N1.GND, LCM1602_IIC1.GND, VCC1.-, U1.G$1_A
  N5: Part1.D6_PWM, L298N1.IN1, S1.L1
  5V: Part1.5V, M1.VIN, Part2.+5V, LCM1602_IIC1.VCC, U1.G$2_2
  N6: Part1.VIN, L298N1.5V#7, S1.COM
  N7: L298N1.OUT1, M2.pin_2
  N8: L298N1.OUT2, M2.pin_1
  N9: L298N1.12V, VCC1.+
  N10: L298N1.5V#10, L298N1.ENB
  VSS: LCM1602_IIC1.VSS, LCD1.VSS
  VDD: LCM1602_IIC1.VDD, LCD1.VDD
  N11: LCM1602_IIC1.V0, LCD1.V0
  N12: LCM1602_IIC1.RS, LCD1.RS
  N13: LCM1602_IIC1.RW, LCD1.R/W
  N14: LCM1602_IIC1.E, LCD1.E
  N15: LCM1602_IIC1.D0, LCD1.DB0
  N16: LCM1602_IIC1.D1, LCD1.DB1
  N17: LCM1602_IIC1.D2, LCD1.DB2
  N18: LCM1602_IIC1.D3, LCD1.DB3
  N19: LCM1602_IIC1.D4, LCD1.DB4
  N20: LCM1602_IIC1.D5, LCD1.DB5
  N21: LCM1602_IIC1.D6, LCD1.DB6
  N22: LCM1602_IIC1.D7, LCD1.DB7
  N23: LCM1602_IIC1.A, LCD1.LED+
  N24: LCM1602_IIC1.K, LCD1.LED-
  N25: LCM1602_IIC1.LED_A, LCM1602_IIC1.LED_B

notes:
  HeartRate sensor
  BMP180 temp sensor
  I2C lcd module
  Speed control POT
  L298N Motor Driver
  Diaphram Pump Motor
  LCD Display, BPM, TMP, O2

custom parts:
  MAX30102: Oximeter module using the MAX30102 chip. You may wish to read (and check your module) this post on power problems with these modules: https://reedpaper.wordpress.com/2018/08/22/pulse-oximeter-max30100-max30102-how-to-fix-wrong-board/ . As usual, if you want the mounting holes in pcb, you need to drag a hole over the pad in silkscreen to actually drill the hole (by default they are not drilled)
  Adafruit BMP180: This precision sensor from Bosch is the best low-cost sensing solution for measuring barometric pressure and temperature. Because pressure changes with altitude you can also use it as an altimeter! The sensor is soldered onto a PCB with a 3.3V regulator, I2C level shifter and pull-up resistors on the I2C pins. The BMP180 is the next-generation of sensors from Bosch, and replaces the BMP085.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
  L298N DC motor driver: 2x DC motor driver with 78M05 positive voltage regulator (7..35 V) L298N: max 46 V, 2 A Set 5 V Enable jumper to enable 5 V regultor (needed for the L298N) and +5 V output at screw terminal or supply external +5 V at screw terminal Set ENA and/or ENB to +5 V to enable motor permanently or supply ENA and/or ENB with PWM signal IN1 and IN2 set rotation directory for motor A (OUT1/OUT2) IN2 and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
  LCM1602 IIC: I2C-Module to use a 1602 or 2004 LCD on with the wire.h libory Serial LCD Modul
